// Logisim project LiuProject1.circ as structural Verilog: 1 circuit, main circuit main
module main (
  input  A,
  input  B,
  input  C,
  output F
);

  wire A_AND_NOT_B_out, B_AND_C_out, not_1_out;

  not not_1 (not_1_out, B);
  and A_AND_NOT_B (A_AND_NOT_B_out, A, not_1_out);
  and B_AND_C (B_AND_C_out, B, C);
  or or_1 (F, A_AND_NOT_B_out, B_AND_C_out);
endmodule
